# Fritzing sketch Circuit (saved by Fritzing 0.9.3b)
breadboards: 1

parts:
  Part1 = Arduino Uno (Rev3)
  Color_Sensor = Color Sensor Breakout ADJD-S311
  Toggle_Switch = Taiway 100-SP-X-T1 SPDT Miniature Toggle Switch [part_number=100-SP-X-T1-0-0-B1-M1 package=THT]
  R1 = Resistor [tolerance=±5% resistance=100 package="1206 [SMD]"]
  Encoder = Hexadecimal Rotary Encoder [part_number=APEM-PT65-303 package=THT]
  Limit_Switch = LilyPad Slide Switch
  R2 = Resistor [tolerance=±5% resistance=100 package="1206 [SMD]"]
  Part2 = Monster Moto Shield
  VCC1 = Battery
  M1 = DC Motor

nets:
  N1: Part1.A3, Color_Sensor.SCL
  N2: Part1.A4/SDA, Color_Sensor.SDA
  N3: Part1.D8, Limit_Switch.ON, R2.Pin_0
  N4: Part1.D9_PWM, Part2.EN2_-_A1
  N5: Part1.D10_PWM/SS, Part2.CS1_-_A2
  N6: Part1.D11_PWM/MOSI, Part2.CS2_-_A3
  N7: Part1.D2, Encoder.InputCommon2
  N8: Part1.D3_PWM, Encoder.Output4Pin
  N9: Part1.D5_PWM, Toggle_Switch.COM, R1.Pin_1
  N10: Color_Sensor.LED, Color_Sensor.VCC
  N11: Color_Sensor.SLP, Encoder.Output8pin, Limit_Switch.OFF
  GND: Color_Sensor.GND, Toggle_Switch.L1, R1.Pin_0, Encoder.Output2Pin, R2.Pin_1, Part2.GND, Part2.GND_-_GND@1, VCC1.-
  N12: Part2.OUTA1, M1.pin_1
  N13: Part2.OUTB1, M1.pin_2
  N14: Part2.VCC, VCC1.+

notes:
  Right Chute
  Left Chute
  Drop Requerst
